// Logisim project 我的cpu+最终版1(1).circ as structural Verilog: 15 circuits, main circuit main
module main (
  input  in_1,
  output [5:0] func,
  output [5:0] opcode
);

  wire _1, _1_prime, _1_prime_prime, _2, _2_prime, _2_prime_prime, _3, _3_prime, _3_prime_prime, _4,
       _4_prime, _4_prime_prime, _5, _5_prime, _5_prime_prime, _6, _6_prime, _6_prime_prime, _7, _7_prime,
       _7_prime_prime, ALUSrc, Branch, clk, \final , J, MemRead, MemToReg, MemWrite, PCSrc_out, RegDst,
       RegWrite, ZERO;
  wire [1:0] ALUOp_1_0, ExtOp_1_0;
  wire [4:0] multiplexer_1_out, PCaddress, \rs源1 , \rt源2 ;
  wire [15:6] address;
  wire [31:0] alu_1_result, extender_1_ext32, multiplexer_2_out, multiplexer_3_out, ram_1_data,
       \regfile_1_d1读出的寄存器数据 , \regfile_1_d2读出的寄存器数据 ;

  _7_segment1 u_7_segment1_1 (
    .A4(PCaddress[4]), .A3(PCaddress[3]), .A2(PCaddress[2]), .A1(PCaddress[1]), .A0(PCaddress[0]), .a(_1),
    .b(_2), .c(_3), .d(_4), .e(_5), .f(_6), .g(_7));
  _7_segment2 u_7_segment2_1 (
    .A4(PCaddress[4]), .A3(PCaddress[3]), .A2(PCaddress[2]), .A1(PCaddress[1]), .A0(PCaddress[0]),
    .a(_1_prime), .b(_2_prime), .c(_3_prime), .d(_4_prime), .e(_5_prime), .f(_6_prime), .g(_7_prime));
  _7_segmentEnd u_7_segmentend_1 (
    .A0(\final ), .a(_1_prime_prime), .b(_2_prime_prime), .c(_3_prime_prime), .d(_4_prime_prime),
    .e(_5_prime_prime), .f(_6_prime_prime), .g(_7_prime_prime));
  Clock clock_1 (.out(clk));
  _7_Segment_Display u_7_segment_display_1 (
    .g(_7_prime), .f(_6_prime), .a(_1_prime), .b(_2_prime), .e(_5_prime), .d(_4_prime), .c(_3_prime));  // open: dp
  _7_Segment_Display u_7_segment_display_2 (
    .g(_7_prime_prime), .f(_6_prime_prime), .a(_1_prime_prime), .b(_2_prime_prime), .e(_5_prime_prime),
    .d(_4_prime_prime), .c(_3_prime_prime));  // open: dp
  and PCSrc (PCSrc_out, ZERO, Branch);
  _7_Segment_Display u_7_segment_display_3 (.g(_7), .f(_6), .a(_1), .b(_2), .e(_5), .d(_4), .c(_3));  // open: dp
  IFU ifu_1 (
    .PCSrc(PCSrc_out), .\reset复位 (in_1), .\输出到main_取出的指令 ({opcode, \rs源1 , \rt源2 , address, func}),
    .\clk时钟 (clk), .J(J), .PCaddress(PCaddress));
  // Probe on {opcode, \rs源1 , \rt源2 , address, func}
  // Probe on PCaddress
  // Probe on {opcode, \rs源1 , \rt源2 , address, func}
  Comparator #(.width(32)) comparator_1 (
    .a({opcode, \rs源1 , \rt源2 , address, func}), .b({32{1'b0}}), .eq(\final ));  // open: gt, lt
  Multiplexer #(.width(5)) multiplexer_1 (
    .in0(\rt源2 ), .in1(address[15:11]), .out(multiplexer_1_out), .sel(RegDst));  // open: en
  Controller controller_1 (
    .func(func), .opcode(opcode), .RegDst(RegDst), .ALUSrc(ALUSrc), .MemtoReg(MemToReg), .RegWrite(RegWrite),
    .Memread(MemRead), .MemWrite(MemWrite), .Branch(Branch), .ALUOp_1_0(ALUOp_1_0), .ExtOp_1_0(ExtOp_1_0),
    .J(J));
  Extender extender_1 (.imm16({address, func}), .ExtOp_1_0(ExtOp_1_0), .ext32(extender_1_ext32));
  RegFile regfile_1 (
    .clk(clk), .\A1_读寄存器 (\rs源1 ), .\A2_读寄存器 (\rt源2 ), .\A3_写寄存器 (multiplexer_1_out),
    .\WD要写的数据 (multiplexer_3_out), .\D1读出的寄存器数据 (\regfile_1_d1读出的寄存器数据 ),
    .\D2读出的寄存器数据 (\regfile_1_d2读出的寄存器数据 ), .RegWrite(RegWrite));
  Multiplexer #(.width(32)) multiplexer_2 (
    .in0(\regfile_1_d2读出的寄存器数据 ), .in1(extender_1_ext32), .out(multiplexer_2_out), .sel(ALUSrc));  // open: en
  Multiplexer #(.width(32)) multiplexer_3 (
    .in0(alu_1_result), .in1(ram_1_data), .out(multiplexer_3_out), .sel(MemToReg));  // open: en
  ALU alu_1 (
    .A(\regfile_1_d1读出的寄存器数据 ), .B(multiplexer_2_out), .ALUOp(ALUOp_1_0), .\判断ALU输出是否为0 (ZERO),
    .Result(alu_1_result));
  RAM #(.addrWidth(5), .dataWidth(32), .bus("separate")) ram_1 (
    .addr(alu_1_result[4:0]), .din(\regfile_1_d2读出的寄存器数据 ), .data(ram_1_data), .str(MemWrite), .clk(clk),
    .clr(in_1));  // open: sel, ld

  // Other names for the same wires on the sheet: address[5:0] = func; shamt[4:0] = address[10:6];
  //   rd[4:0] = address[15:11]; reset = in_1

  // Notes on the sheet:
  //   执行结束标志
  //   显示当前指令行号
  //   取指令单元
  //   0：未结束
  //   1：结束
  //   低
  //   func
  //   shamt
  //   rd
  //   rt
  //   rs
  //   opcode
  //   高
  //   address
  //   r指令时指出alu功能
  //   寄存器堆
  //   ↑要写入寄存器的数据
  //   ←要写入寄存器的数据
  //   寄存器读出的数据2
  //   指令低16位的符号拓展
  //   控制PC是否转移到J指令指示的地址
  //   控制Extender的拓展方式
  //   2 bit 控制ALU的运算
  //   与ALU0输出结合决定PC是否跳转
  //   将数据写入到指定存储器单元中
  //   寄存器写使能有效
  //   写入寄存器的数据来源
  //   第二个ALU操作数的来源
  //   写寄存器的目标寄存器号来源
  //   寄存器读出的数据2→送往内存单元
  //   没用到  Mem可以随时read
  //   内存地址 为什么是这五位?
  //   因为RAM32bit*32字 地址只能寻2^5
  //   所以内存地址只能取这5位
  //   注意以字寻址
  //   如果有更大的RAM 地址可以更长
  //   RAM(DM)
endmodule

module ALU (
  input  [31:0] A,
  input  [31:0] B,
  input  [1:0] ALUOp,
  output \判断ALU输出是否为0 ,
  output [31:0] Result
);

  wire [31:0] _32_bit_Adder_sum, _32_bit_ori_out_3, _32_bit_substract_out_3;

  _32_bit_Adder _32_bit_Adder (.B(B), .A(A), .Sum(_32_bit_Adder_sum));
  _32_bit_Substract _32_bit_substract (.\A被减数 (A), .\B减数 (B), .out_3(_32_bit_substract_out_3));
  _32_bit_ori _32_bit_ori (.A(A), .B(B), .out_3(_32_bit_ori_out_3));
  Multiplexer #(.select(2), .width(32)) multiplexer_1 (
    .in0(_32_bit_Adder_sum), .in1(_32_bit_substract_out_3), .in2(_32_bit_ori_out_3), .out(Result), .sel(ALUOp));  // open: in3, en
  Comparator #(.width(32)) comparator_1 (.a(Result), .b({32{1'b0}}), .eq(\判断ALU输出是否为0 ));  // open: gt, lt

  // Notes on the sheet:
  //   alu控制信号 控制输出哪一个结果
  //   0 0 add
  //   0 1 sub
  //   1 0 or
endmodule

module _32_bit_Adder (
  input  [31:0] B,
  input  [31:0] A,
  output [31:0] Sum
);

  wire \_0_c进位 , \_1_进位c_i_1 , \_2_进位c_i_1 , \_3_进位c_i_1 , \_4_进位c_i_1 , \_5_进位c_i_1 , \_6_进位c_i_1 ,
       \_7_进位c_i_1 , \_8_进位c_i_1 , \_9_进位c_i_1 , \_10_进位c_i_1 , \_11_进位c_i_1 , \_12_进位c_i_1 , \_13_进位c_i_1 ,
       \_14_进位c_i_1 , \_15_进位c_i_1 , \_16_进位c_i_1 , \_17_进位c_i_1 , \_18_进位c_i_1 , \_19_进位c_i_1 ,
       \_20_进位c_i_1 , \_21_进位c_i_1 , \_22_进位c_i_1 , \_23_进位c_i_1 , \_24_进位c_i_1 , \_25_进位c_i_1 ,
       \_26_进位c_i_1 , \_27_进位c_i_1 , \_28_进位c_i_1 , \_29_进位c_i_1 , \_30_进位c_i_1 ;

  \_1位全加器_3输入_2输出  _31 (.a_i(A[31]), .b_i(B[31]), .c_i(\_30_进位c_i_1 ), .\结果s_i (Sum[31]));  // open: 进位c_i_1
  \_1位全加器_3输入_2输出  _30 (.a_i(A[30]), .b_i(B[30]), .c_i(\_29_进位c_i_1 ), .\结果s_i (Sum[30]), .\进位c_i_1 (\_30_进位c_i_1 ));
  \_1位全加器_3输入_2输出  _29 (.a_i(A[29]), .b_i(B[29]), .c_i(\_28_进位c_i_1 ), .\结果s_i (Sum[29]), .\进位c_i_1 (\_29_进位c_i_1 ));
  \_1位全加器_3输入_2输出  _28 (.a_i(A[28]), .b_i(B[28]), .c_i(\_27_进位c_i_1 ), .\结果s_i (Sum[28]), .\进位c_i_1 (\_28_进位c_i_1 ));
  \_1位全加器_3输入_2输出  _27 (.a_i(A[27]), .b_i(B[27]), .c_i(\_26_进位c_i_1 ), .\结果s_i (Sum[27]), .\进位c_i_1 (\_27_进位c_i_1 ));
  \_1位全加器_3输入_2输出  _26 (.a_i(A[26]), .b_i(B[26]), .c_i(\_25_进位c_i_1 ), .\结果s_i (Sum[26]), .\进位c_i_1 (\_26_进位c_i_1 ));
  \_1位全加器_3输入_2输出  _25 (.a_i(A[25]), .b_i(B[25]), .c_i(\_24_进位c_i_1 ), .\结果s_i (Sum[25]), .\进位c_i_1 (\_25_进位c_i_1 ));
  \_1位全加器_3输入_2输出  _24 (.a_i(A[24]), .b_i(B[24]), .c_i(\_23_进位c_i_1 ), .\结果s_i (Sum[24]), .\进位c_i_1 (\_24_进位c_i_1 ));
  \_1位全加器_3输入_2输出  _23 (.a_i(A[23]), .b_i(B[23]), .c_i(\_22_进位c_i_1 ), .\结果s_i (Sum[23]), .\进位c_i_1 (\_23_进位c_i_1 ));
  \_1位全加器_3输入_2输出  _22 (.a_i(A[22]), .b_i(B[22]), .c_i(\_21_进位c_i_1 ), .\结果s_i (Sum[22]), .\进位c_i_1 (\_22_进位c_i_1 ));
  \_1位全加器_3输入_2输出  _21 (.a_i(A[21]), .b_i(B[21]), .c_i(\_20_进位c_i_1 ), .\结果s_i (Sum[21]), .\进位c_i_1 (\_21_进位c_i_1 ));
  \_1位全加器_3输入_2输出  _20 (.a_i(A[20]), .b_i(B[20]), .c_i(\_19_进位c_i_1 ), .\结果s_i (Sum[20]), .\进位c_i_1 (\_20_进位c_i_1 ));
  \_1位全加器_3输入_2输出  _19 (.a_i(A[19]), .b_i(B[19]), .c_i(\_18_进位c_i_1 ), .\结果s_i (Sum[19]), .\进位c_i_1 (\_19_进位c_i_1 ));
  \_1位全加器_3输入_2输出  _18 (.a_i(A[18]), .b_i(B[18]), .c_i(\_17_进位c_i_1 ), .\结果s_i (Sum[18]), .\进位c_i_1 (\_18_进位c_i_1 ));
  \_1位全加器_3输入_2输出  _17 (.a_i(A[17]), .b_i(B[17]), .c_i(\_16_进位c_i_1 ), .\结果s_i (Sum[17]), .\进位c_i_1 (\_17_进位c_i_1 ));
  \_1位全加器_3输入_2输出  _16 (.a_i(A[16]), .b_i(B[16]), .c_i(\_15_进位c_i_1 ), .\结果s_i (Sum[16]), .\进位c_i_1 (\_16_进位c_i_1 ));
  \_1位全加器_3输入_2输出  _15 (.a_i(A[15]), .b_i(B[15]), .c_i(\_14_进位c_i_1 ), .\结果s_i (Sum[15]), .\进位c_i_1 (\_15_进位c_i_1 ));
  \_1位全加器_3输入_2输出  _14 (.a_i(A[14]), .b_i(B[14]), .c_i(\_13_进位c_i_1 ), .\结果s_i (Sum[14]), .\进位c_i_1 (\_14_进位c_i_1 ));
  \_1位全加器_3输入_2输出  _13 (.a_i(A[13]), .b_i(B[13]), .c_i(\_12_进位c_i_1 ), .\结果s_i (Sum[13]), .\进位c_i_1 (\_13_进位c_i_1 ));
  \_1位全加器_3输入_2输出  _12 (.a_i(A[12]), .b_i(B[12]), .c_i(\_11_进位c_i_1 ), .\结果s_i (Sum[12]), .\进位c_i_1 (\_12_进位c_i_1 ));
  \_1位全加器_3输入_2输出  _11 (.a_i(A[11]), .b_i(B[11]), .c_i(\_10_进位c_i_1 ), .\结果s_i (Sum[11]), .\进位c_i_1 (\_11_进位c_i_1 ));
  \_1位全加器_3输入_2输出  _10 (.a_i(A[10]), .b_i(B[10]), .c_i(\_9_进位c_i_1 ), .\结果s_i (Sum[10]), .\进位c_i_1 (\_10_进位c_i_1 ));
  \_1位全加器_3输入_2输出  _9 (.a_i(A[9]), .b_i(B[9]), .c_i(\_8_进位c_i_1 ), .\结果s_i (Sum[9]), .\进位c_i_1 (\_9_进位c_i_1 ));
  \_1位全加器_3输入_2输出  _8 (.a_i(A[8]), .b_i(B[8]), .c_i(\_7_进位c_i_1 ), .\结果s_i (Sum[8]), .\进位c_i_1 (\_8_进位c_i_1 ));
  \_1位全加器_3输入_2输出  _7 (.a_i(A[7]), .b_i(B[7]), .c_i(\_6_进位c_i_1 ), .\结果s_i (Sum[7]), .\进位c_i_1 (\_7_进位c_i_1 ));
  \_1位全加器_3输入_2输出  _6 (.a_i(A[6]), .b_i(B[6]), .c_i(\_5_进位c_i_1 ), .\结果s_i (Sum[6]), .\进位c_i_1 (\_6_进位c_i_1 ));
  \_1位全加器_3输入_2输出  _5 (.a_i(A[5]), .b_i(B[5]), .c_i(\_4_进位c_i_1 ), .\结果s_i (Sum[5]), .\进位c_i_1 (\_5_进位c_i_1 ));
  \_1位全加器_3输入_2输出  _4 (.a_i(A[4]), .b_i(B[4]), .c_i(\_3_进位c_i_1 ), .\结果s_i (Sum[4]), .\进位c_i_1 (\_4_进位c_i_1 ));
  \_1位全加器_3输入_2输出  _3 (.a_i(A[3]), .b_i(B[3]), .c_i(\_2_进位c_i_1 ), .\结果s_i (Sum[3]), .\进位c_i_1 (\_3_进位c_i_1 ));
  \_1位全加器_3输入_2输出  _2 (.a_i(A[2]), .b_i(B[2]), .c_i(\_1_进位c_i_1 ), .\结果s_i (Sum[2]), .\进位c_i_1 (\_2_进位c_i_1 ));
  \_1位全加器_3输入_2输出  _1 (.a_i(A[1]), .b_i(B[1]), .c_i(\_0_c进位 ), .\结果s_i (Sum[1]), .\进位c_i_1 (\_1_进位c_i_1 ));
  \_1位半加器_2输入_2输出  _0 (.A(B[0]), .B(A[0]), .\sum和 (Sum[0]), .\C进位 (\_0_c进位 ));

  // Other names for the same wires on the sheet: s0 = Sum[0]; s1 = Sum[1]; s2 = Sum[2]; s3 = Sum[3]; s4 = Sum[4];
  //   s5 = Sum[5]; s6 = Sum[6]; s7 = Sum[7]; s8 = Sum[8]; s9 = Sum[9]; s10 = Sum[10]; s11 = Sum[11]; s12 = Sum[12];
  //   s13 = Sum[13]; s14 = Sum[14]; s15 = Sum[15]; s16 = Sum[16]; s17 = Sum[17]; s18 = Sum[18]; s19 = Sum[19];
  //   s20 = Sum[20]; s21 = Sum[21]; s22 = Sum[22]; s23 = Sum[23]; s24 = Sum[24]; s25 = Sum[25]; s26 = Sum[26];
  //   s27 = Sum[27]; s28 = Sum[28]; s29 = Sum[29]; s30 = Sum[30]; s31 = Sum[31]
endmodule

module \_1位全加器_3输入_2输出  (
  input  a_i,
  input  b_i,
  input  c_i,
  output \结果s_i ,
  output \进位c_i_1 
);

  xor xor_1 (\结果s_i , a_i, b_i, c_i);
  \判断是否进位_3输入_1输出  \u_判断是否进位_3输入_1输出_1  (.in_1(a_i), .in_2(b_i), .in_3(c_i), .out_4(\进位c_i_1 ));

  // Notes on the sheet:
  //   判断是否进位
endmodule

module \_1位半加器_2输入_2输出  (
  input  A,
  input  B,
  output \sum和 ,
  output \C进位 
);

  xor xor_1 (\sum和 , A, B);
  and and_1 (\C进位 , A, B);

  // Notes on the sheet:
  //   1 bit adder
  //   半加器 两个1位2进制数相加不考虑低位进位
endmodule

module \判断是否进位_3输入_1输出  (
  input  in_1,
  input  in_2,
  input  in_3,
  output out_4
);

  wire and_1_out, and_2_out, and_3_out;

  and and_1 (and_1_out, in_1, in_2);
  and and_2 (and_2_out, in_1, in_3);
  and and_3 (and_3_out, in_2, in_3);
  or or_1 (out_4, and_1_out, and_2_out, and_3_out);
endmodule

module _32_bit_Substract (
  input  [31:0] \A被减数 ,
  input  [31:0] \B减数 ,
  output [31:0] out_3
);

  wire [31:0] _32_bit_Adder_sum, not_1_out;

  assign not_1_out = ~\B减数 ;  // NOT_Gate not_1, 32 bits wide
  _32_bit_Adder _32_bit_Adder (.B(32'h1), .A(not_1_out), .Sum(_32_bit_Adder_sum));
  _32_bit_Adder _32_bit_Adder_2 (.B(_32_bit_Adder_sum), .A(\A被减数 ), .Sum(out_3));

  // Notes on the sheet:
  //   A
  //   B
endmodule

module _32_bit_ori (
  input  [31:0] A,
  input  [31:0] B,
  output [31:0] out_3
);

  assign out_3 = A | B;  // OR_Gate or_1, 32 bits wide
endmodule

module IFU (
  input  J,
  input  PCSrc,
  input  \clk时钟 ,
  input  \reset复位 ,
  output [4:0] PCaddress,
  output [31:0] \输出到main_取出的指令 
);

  wire _26, _27, _28, _29;
  wire [25:5] register_1_q;
  wire [29:0] multiplexer_2_out;
  wire [31:0] Adder_2_sum, Adder_sum, bit_extender_1_out, multiplexer_1_out;
  wire [31:30] multiplexer_2_out_2;

  Register #(.width(30)) register_1 (
    .D(multiplexer_2_out), .Q({_29, _28, _27, _26, register_1_q, PCaddress}), .clk(\clk时钟 ), .clr(\reset复位 ));  // open: en
  _32_bit_Adder Adder (.B(32'h1), .A({2'b00, _29, _28, _27, _26, register_1_q, PCaddress}), .Sum(Adder_sum));
  ROM #(.addrWidth(5), .dataWidth(32)) rom_1 (.addr(PCaddress), .data(\输出到main_取出的指令 ));  // open: sel
  assign bit_extender_1_out = {{16{1'b0}}, \输出到main_取出的指令 [15:0]};  // Bit_Extender bit_extender_1
  _32_bit_Adder Adder_2 (.B(bit_extender_1_out), .A(Adder_sum), .Sum(Adder_2_sum));
  Multiplexer #(.width(32)) multiplexer_1 (
    .in0(Adder_sum), .in1(Adder_2_sum), .out(multiplexer_1_out), .sel(PCSrc));  // open: en
  Multiplexer #(.width(32)) multiplexer_2 (
    .in0(multiplexer_1_out), .in1({2'b00, _29, _28, _27, _26, \输出到main_取出的指令 [25:0]}),
    .out({multiplexer_2_out_2, multiplexer_2_out}), .sel(J));  // open: en

  // Notes on the sheet:
  //   PC
  //   30 bit register
  //   30 to 32
  //   高位补0
  //   指令地址
  //   跳转地址的高4位来自于跳转指令的PC+4
  //   (指示当前区域，只能在当前区域内跳转)
  //   PC+1
  //   以字寻址 所以加一即可达到加4的效果
  //   IM 指令存储器
  //   ROM 32bit*32字
  //   32 bit 指令
  //   contents of rom_1 (hex, n*v repeats v):
  //   3c0800ff 3c090001 1095021 1495023 350b5555 3c0c0001 3c0d0001 35ad0001 1ac6023 1ec4021 1084021
  //   1084021 1ef4821 18c6821 1ad6821 1ac6821 1ac7021 1cc7821 12c4821 11090001 810000f 3c080000 ad0c0000
  //   8d0d0000
  //   位扩展：16 to 32
  //   取偏移地址
  //   offset 16 bit
  //   以字为单位
  //   以字为单位
  //   PC+4
  //   offset
  //   PC+4+offset
  //   J指令专用splitter（其实可以和左侧合并）
  //   高位补0
  //   PC+4→
  //   PC+4+offset
  //   判断是否执行分支
  //   判断是否J指令
  //   32 to30
endmodule

module Controller (
  input  [5:0] func,
  input  [5:0] opcode,
  output J,
  output RegDst,
  output ALUSrc,
  output MemtoReg,
  output RegWrite,
  output Memread,
  output MemWrite,
  output Branch,
  output [1:0] ALUOp_1_0,
  output [1:0] ExtOp_1_0
);

  wire ADDU_out, BEQ_out, J_out, LW_out, not_1_out, not_2_out, not_3_out, not_4_out, not_5_out, not_6_out,
       not_7_out, not_8_out, not_9_out, not_10_out, not_11_out, not_12_out, ORI_out, SUBU_out, SW_out;

  not not_1 (not_1_out, func[5]);
  not not_2 (not_2_out, func[4]);
  not not_3 (not_3_out, func[3]);
  not not_4 (not_4_out, func[2]);
  not not_5 (not_5_out, func[1]);
  not not_6 (not_6_out, func[0]);
  not not_7 (not_7_out, opcode[5]);
  not not_8 (not_8_out, opcode[4]);
  not not_9 (not_9_out, opcode[3]);
  not not_10 (not_10_out, opcode[1]);
  not not_11 (not_11_out, opcode[2]);
  not not_12 (not_12_out, opcode[0]);
  and ADDU (ADDU_out, func[5], not_2_out, not_3_out, not_4_out, not_5_out, func[0], not_7_out, not_8_out, not_9_out, not_11_out, not_10_out, not_12_out);
  and SUBU (SUBU_out, func[5], not_2_out, not_3_out, not_4_out, func[1], func[0], not_7_out, not_8_out, not_9_out, not_11_out, not_10_out, not_12_out);
  and ORI (ORI_out, not_7_out, not_8_out, opcode[3], opcode[2], not_10_out, opcode[0]);
  and LW (LW_out, opcode[5], not_8_out, not_9_out, not_11_out, opcode[1], opcode[0]);
  and SW (SW_out, opcode[5], not_8_out, opcode[3], not_11_out, opcode[1], opcode[0]);
  and BEQ (BEQ_out, not_7_out, not_8_out, not_9_out, opcode[2], not_10_out, not_12_out);
  and LUI (ExtOp_1_0[1], not_7_out, not_8_out, opcode[3], opcode[2], opcode[1], opcode[0]);
  and u_J (J_out, not_7_out, not_8_out, not_9_out, not_11_out, opcode[1], not_12_out);
  or u_RegDst (RegDst, ADDU_out, SUBU_out);
  or u_ALUSrc (ALUSrc, ORI_out, LW_out, SW_out, ExtOp_1_0[1]);
  buf u_MemtoReg (MemtoReg, LW_out);  // OR_Gate
  or u_RegWrite (RegWrite, ADDU_out, SUBU_out, ExtOp_1_0[1], ORI_out, LW_out);
  buf u_Memread (Memread, LW_out);  // OR_Gate
  buf u_MemWrite (MemWrite, SW_out);  // OR_Gate
  buf u_Branch (Branch, BEQ_out);  // OR_Gate
  buf ALUOp1 (ALUOp_1_0[1], ORI_out);  // OR_Gate
  or ALUOp0 (ALUOp_1_0[0], SUBU_out, BEQ_out);
  or ExtOp_0 (ExtOp_1_0[0], LW_out, SW_out);
  buf J_2 (J, J_out);  // OR_Gate

  // Notes on the sheet:
  //   0
  //   1
  //   000000addu   000000subu   001101ori   100011lw   101011sw   000100beq   001111lui    000010j
  //   0
  //   1
  //   ?
  //   当ALUOp为00或01时，ALU动作不依赖于func字段
  //   4位的ALU控制信号有什么用？ALUOp不就可以解决了吗？
endmodule

// RegFile(GPR)
module RegFile (
  input  clk,
  input  RegWrite,
  input  [4:0] \A1_读寄存器 ,
  input  [4:0] \A2_读寄存器 ,
  input  [4:0] \A3_写寄存器 ,
  input  [31:0] \WD要写的数据 ,
  output [31:0] \D1读出的寄存器数据 ,
  output [31:0] \D2读出的寄存器数据 
);

  wire demultiplexer_1_out0, demultiplexer_1_out1, demultiplexer_1_out2, demultiplexer_1_out3,
       demultiplexer_1_out4, demultiplexer_1_out5, demultiplexer_1_out6, demultiplexer_1_out7,
       demultiplexer_1_out8, demultiplexer_1_out9, demultiplexer_1_out10, demultiplexer_1_out11,
       demultiplexer_1_out12, demultiplexer_1_out13, demultiplexer_1_out14, demultiplexer_1_out15,
       demultiplexer_1_out16, demultiplexer_1_out17, demultiplexer_1_out18, demultiplexer_1_out19,
       demultiplexer_1_out20, demultiplexer_1_out21, demultiplexer_1_out22, demultiplexer_1_out23,
       demultiplexer_1_out24, demultiplexer_1_out25, demultiplexer_1_out26, demultiplexer_1_out27,
       demultiplexer_1_out28, demultiplexer_1_out29, demultiplexer_1_out30, demultiplexer_1_out31;
  wire [31:0] _0, _1, _2, _3, _4, _5, _6, _7, _8, _9, _10, _11, _12, _13, _14, _15, _16, _17, _18, _19, _20,
       _21, _22, _23, _24, _25, _26, _27, _28, _29, _30, _31;

  Demultiplexer #(.select(5)) demultiplexer_1 (
    .out0(demultiplexer_1_out0), .out1(demultiplexer_1_out1), .out2(demultiplexer_1_out2),
    .out3(demultiplexer_1_out3), .out4(demultiplexer_1_out4), .out5(demultiplexer_1_out5),
    .out6(demultiplexer_1_out6), .out7(demultiplexer_1_out7), .out8(demultiplexer_1_out8),
    .out9(demultiplexer_1_out9), .out10(demultiplexer_1_out10), .out11(demultiplexer_1_out11),
    .out12(demultiplexer_1_out12), .out13(demultiplexer_1_out13), .out14(demultiplexer_1_out14),
    .out15(demultiplexer_1_out15), .out16(demultiplexer_1_out16), .out17(demultiplexer_1_out17),
    .out18(demultiplexer_1_out18), .out19(demultiplexer_1_out19), .out20(demultiplexer_1_out20),
    .out21(demultiplexer_1_out21), .out22(demultiplexer_1_out22), .out23(demultiplexer_1_out23),
    .out24(demultiplexer_1_out24), .out25(demultiplexer_1_out25), .out26(demultiplexer_1_out26),
    .out27(demultiplexer_1_out27), .out28(demultiplexer_1_out28), .out29(demultiplexer_1_out29),
    .out30(demultiplexer_1_out30), .out31(demultiplexer_1_out31), .in(RegWrite), .sel(\A3_写寄存器 ));  // open: en
  Register #(.width(32)) register_1 (.D(\WD要写的数据 ), .en(demultiplexer_1_out0), .Q(_0), .clk(clk));  // open: clr
  Register #(.width(32)) register_2 (.D(\WD要写的数据 ), .en(demultiplexer_1_out1), .Q(_1), .clk(clk));  // open: clr
  Register #(.width(32)) register_3 (.D(\WD要写的数据 ), .en(demultiplexer_1_out2), .Q(_2), .clk(clk));  // open: clr
  Register #(.width(32)) register_4 (.D(\WD要写的数据 ), .en(demultiplexer_1_out3), .Q(_3), .clk(clk));  // open: clr
  Register #(.width(32)) register_5 (.D(\WD要写的数据 ), .en(demultiplexer_1_out4), .Q(_4), .clk(clk));  // open: clr
  Register #(.width(32)) register_6 (.D(\WD要写的数据 ), .en(demultiplexer_1_out5), .Q(_5), .clk(clk));  // open: clr
  Register #(.width(32)) register_7 (.D(\WD要写的数据 ), .en(demultiplexer_1_out6), .Q(_6), .clk(clk));  // open: clr
  Register #(.width(32)) register_8 (.D(\WD要写的数据 ), .en(demultiplexer_1_out7), .Q(_7), .clk(clk));  // open: clr
  Register #(.width(32)) register_9 (.D(\WD要写的数据 ), .en(demultiplexer_1_out8), .Q(_8), .clk(clk));  // open: clr
  Register #(.width(32)) register_10 (.D(\WD要写的数据 ), .en(demultiplexer_1_out9), .Q(_9), .clk(clk));  // open: clr
  Register #(.width(32)) register_11 (.D(\WD要写的数据 ), .en(demultiplexer_1_out10), .Q(_10), .clk(clk));  // open: clr
  Register #(.width(32)) register_12 (.D(\WD要写的数据 ), .en(demultiplexer_1_out11), .Q(_11), .clk(clk));  // open: clr
  Register #(.width(32)) register_13 (.D(\WD要写的数据 ), .en(demultiplexer_1_out12), .Q(_12), .clk(clk));  // open: clr
  Register #(.width(32)) register_14 (.D(\WD要写的数据 ), .en(demultiplexer_1_out13), .Q(_13), .clk(clk));  // open: clr
  Register #(.width(32)) register_15 (.D(\WD要写的数据 ), .en(demultiplexer_1_out14), .Q(_14), .clk(clk));  // open: clr
  Register #(.width(32)) register_16 (.D(\WD要写的数据 ), .en(demultiplexer_1_out15), .Q(_15), .clk(clk));  // open: clr
  Register #(.width(32)) register_17 (.D(\WD要写的数据 ), .en(demultiplexer_1_out16), .Q(_16), .clk(clk));  // open: clr
  Register #(.width(32)) register_18 (.D(\WD要写的数据 ), .en(demultiplexer_1_out17), .Q(_17), .clk(clk));  // open: clr
  Register #(.width(32)) register_19 (.D(\WD要写的数据 ), .en(demultiplexer_1_out18), .Q(_18), .clk(clk));  // open: clr
  Register #(.width(32)) register_20 (.D(\WD要写的数据 ), .en(demultiplexer_1_out19), .Q(_19), .clk(clk));  // open: clr
  Register #(.width(32)) register_21 (.D(\WD要写的数据 ), .en(demultiplexer_1_out20), .Q(_20), .clk(clk));  // open: clr
  Register #(.width(32)) register_22 (.D(\WD要写的数据 ), .en(demultiplexer_1_out21), .Q(_21), .clk(clk));  // open: clr
  Register #(.width(32)) register_23 (.D(\WD要写的数据 ), .en(demultiplexer_1_out22), .Q(_22), .clk(clk));  // open: clr
  Register #(.width(32)) register_24 (.D(\WD要写的数据 ), .en(demultiplexer_1_out23), .Q(_23), .clk(clk));  // open: clr
  Register #(.width(32)) register_25 (.D(\WD要写的数据 ), .en(demultiplexer_1_out24), .Q(_24), .clk(clk));  // open: clr
  Register #(.width(32)) register_26 (.D(\WD要写的数据 ), .en(demultiplexer_1_out25), .Q(_25), .clk(clk));  // open: clr
  Register #(.width(32)) register_27 (.D(\WD要写的数据 ), .en(demultiplexer_1_out26), .Q(_26), .clk(clk));  // open: clr
  Register #(.width(32)) register_28 (.D(\WD要写的数据 ), .en(demultiplexer_1_out27), .Q(_27), .clk(clk));  // open: clr
  Register #(.width(32)) register_29 (.D(\WD要写的数据 ), .en(demultiplexer_1_out28), .Q(_28), .clk(clk));  // open: clr
  Register #(.width(32)) register_30 (.D(\WD要写的数据 ), .en(demultiplexer_1_out29), .Q(_29), .clk(clk));  // open: clr
  Register #(.width(32)) register_31 (.D(\WD要写的数据 ), .en(demultiplexer_1_out30), .Q(_30), .clk(clk));  // open: clr
  Register #(.width(32)) register_32 (.D(\WD要写的数据 ), .en(demultiplexer_1_out31), .Q(_31), .clk(clk));  // open: clr
  Multiplexer #(.select(5), .width(32)) multiplexer_1 (
    .in0(_0), .in1(_1), .in2(_2), .in3(_3), .in4(_4), .in5(_5), .in6(_6), .in7(_7), .in8(_8), .in9(_9),
    .in10(_10), .in11(_11), .in12(_12), .in13(_13), .in14(_14), .in15(_15), .in16(_16), .in17(_17),
    .in18(_18), .in19(_19), .in20(_20), .in21(_21), .in22(_22), .in23(_23), .in24(_24), .in25(_25),
    .in26(_26), .in27(_27), .in28(_28), .in29(_29), .in30(_30), .in31(_31), .out(\D1读出的寄存器数据 ),
    .sel(\A1_读寄存器 ));  // open: en
  Multiplexer #(.select(5), .width(32)) multiplexer_2 (
    .in0(_0), .in1(_1), .in2(_2), .in3(_3), .in4(_4), .in5(_5), .in6(_6), .in7(_7), .in8(_8), .in9(_9),
    .in10(_10), .in11(_11), .in12(_12), .in13(_13), .in14(_14), .in15(_15), .in16(_16), .in17(_17),
    .in18(_18), .in19(_19), .in20(_20), .in21(_21), .in22(_22), .in23(_23), .in24(_24), .in25(_25),
    .in26(_26), .in27(_27), .in28(_28), .in29(_29), .in30(_30), .in31(_31), .out(\D2读出的寄存器数据 ),
    .sel(\A2_读寄存器 ));  // open: en

  // Other names for the same wires on the sheet: A1_控制读哪个寄存器[4:0] = \A1_读寄存器 ; A2_控制读哪个寄存器[4:0] = \A2_读寄存器 ;
  //   A3_控制写哪个寄存器[4:0] = \A3_写寄存器 

  // Notes on the sheet:
  //   控制写哪个寄存器
  //   控制读哪个寄存器 可以读两个
  //   这里不加控制信号的话貌似默认随时有效→
  //   Data 要写的数据
  //   控制写哪个寄存器
  //   input
  //   output
  //   $v1
  //   $t0
  //   $zero
  //   $at
  //   $v0
  //   $a0
  //   $a1
  //   $a2
  //   $a3
  //   $t1
  //   $t2
  //   $t3
  //   $t4
  //   $t5
  //   $t6
  //   $t7
  //   $s0
  //   $s1
  //   $s2
  //   $s3
  //   $s4
  //   $s5
  //   $s6
  //   $s7
  //   $t8
  //   $t9
  //   $k0
  //   $k1
  //   $gp
  //   $sp
  //   $fp
  //   $ra
endmodule

module Extender (
  input  [15:0] imm16,
  input  [1:0] ExtOp_1_0,
  output [31:0] ext32
);

  wire [31:0] bit_extender_1_out, bit_extender_2_out;

  assign bit_extender_1_out = {{16{1'b0}}, imm16};  // Bit_Extender bit_extender_1
  assign bit_extender_2_out = {{16{imm16[15]}}, imm16};  // Bit_Extender bit_extender_2
  Multiplexer #(.select(2), .width(32)) multiplexer_1 (
    .in0(bit_extender_1_out), .in1(bit_extender_2_out), .in2({imm16, {16{1'b0}}}), .out(ext32),
    .sel(ExtOp_1_0));  // open: in3, en

  // Notes on the sheet:
  //   低16位补0
  //   lui 拓展到高16位
  //   1 0 拓展到高16位
endmodule

module _7_segment1 (
  input  A4,
  input  A3,
  input  A2,
  input  A1,
  input  A0,
  output a,
  output b,
  output c,
  output d,
  output e,
  output f,
  output g
);

  wire and_1_out, and_2_out, and_3_out, and_4_out, and_5_out, and_6_out, and_7_out, and_8_out, and_9_out,
       and_10_out, and_11_out, and_12_out, and_13_out, and_14_out, and_15_out, and_16_out, and_17_out,
       and_18_out, and_19_out, and_20_out, and_21_out, and_22_out, and_23_out, and_24_out, and_25_out,
       and_26_out, and_27_out, and_28_out, and_29_out, and_30_out, and_31_out, and_32_out, and_33_out,
       and_34_out, and_35_out, and_36_out, and_37_out, and_38_out, and_39_out, and_40_out, and_41_out,
       and_42_out, and_43_out, and_44_out, and_45_out, and_46_out, and_47_out, and_48_out, and_49_out,
       and_50_out, and_51_out, and_52_out, and_53_out, and_54_out, and_55_out, and_56_out, not_1_out,
       not_2_out, not_3_out, not_4_out, not_5_out, not_6_out, not_7_out, not_8_out, not_9_out, not_10_out,
       not_11_out, not_12_out, not_13_out, not_14_out, not_15_out, not_16_out, not_17_out, not_18_out,
       not_19_out, not_20_out, not_21_out, not_22_out, not_23_out, not_24_out, not_25_out, not_26_out,
       not_27_out, not_28_out, not_29_out, not_30_out, not_31_out, not_32_out, not_33_out, not_34_out,
       not_35_out, not_36_out, not_37_out, not_38_out, not_39_out, not_40_out, not_41_out, not_42_out,
       not_43_out, not_44_out, not_45_out, not_46_out, not_47_out, not_48_out, not_49_out, not_50_out,
       not_51_out, not_52_out, not_53_out, not_54_out, not_55_out, not_56_out, not_57_out, not_58_out,
       not_59_out, not_60_out, not_61_out, not_62_out, not_63_out, not_64_out, not_65_out, not_66_out,
       not_67_out, not_68_out, not_69_out, not_70_out, not_71_out, not_72_out, not_73_out, not_74_out,
       not_75_out, not_76_out, not_77_out, not_78_out, not_79_out, not_80_out, not_81_out, not_82_out,
       not_83_out, not_84_out, not_85_out, not_86_out, not_87_out, not_88_out, not_89_out, not_90_out,
       not_91_out, not_92_out, not_93_out, not_94_out, not_95_out, not_96_out, not_97_out, not_98_out;

  not not_1 (not_1_out, A4);
  not not_2 (not_2_out, A2);
  not not_3 (not_3_out, A0);
  not not_4 (not_4_out, A3);
  not not_5 (not_5_out, A4);
  not not_6 (not_6_out, A4);
  not not_7 (not_7_out, A1);
  not not_8 (not_8_out, A1);
  not not_9 (not_9_out, A3);
  not not_10 (not_10_out, A0);
  not not_11 (not_11_out, A2);
  not not_12 (not_12_out, A0);
  not not_13 (not_13_out, A4);
  not not_14 (not_14_out, A2);
  not not_15 (not_15_out, A4);
  not not_16 (not_16_out, A1);
  not not_17 (not_17_out, A0);
  not not_18 (not_18_out, A3);
  not not_19 (not_19_out, A2);
  not not_20 (not_20_out, A3);
  not not_21 (not_21_out, A2);
  not not_22 (not_22_out, A3);
  not not_23 (not_23_out, A2);
  not not_24 (not_24_out, A4);
  not not_25 (not_25_out, A1);
  not not_26 (not_26_out, A4);
  not not_27 (not_27_out, A0);
  not not_28 (not_28_out, A1);
  not not_29 (not_29_out, A0);
  not not_30 (not_30_out, A3);
  not not_31 (not_31_out, A1);
  not not_32 (not_32_out, A2);
  not not_33 (not_33_out, A1);
  not not_34 (not_34_out, A4);
  not not_35 (not_35_out, A3);
  not not_36 (not_36_out, A2);
  not not_37 (not_37_out, A1);
  not not_38 (not_38_out, A4);
  not not_39 (not_39_out, A2);
  not not_40 (not_40_out, A0);
  not not_41 (not_41_out, A3);
  not not_42 (not_42_out, A2);
  not not_43 (not_43_out, A0);
  not not_44 (not_44_out, A3);
  not not_45 (not_45_out, A2);
  not not_46 (not_46_out, A3);
  not not_47 (not_47_out, A0);
  not not_48 (not_48_out, A2);
  not not_49 (not_49_out, A0);
  not not_50 (not_50_out, A4);
  not not_51 (not_51_out, A1);
  not not_52 (not_52_out, A4);
  not not_53 (not_53_out, A1);
  not not_54 (not_54_out, A1);
  not not_55 (not_55_out, A4);
  not not_56 (not_56_out, A3);
  not not_57 (not_57_out, A0);
  not not_58 (not_58_out, A4);
  not not_59 (not_59_out, A2);
  not not_60 (not_60_out, A0);
  not not_61 (not_61_out, A3);
  not not_62 (not_62_out, A2);
  not not_63 (not_63_out, A0);
  not not_64 (not_64_out, A3);
  not not_65 (not_65_out, A0);
  not not_66 (not_66_out, A2);
  not not_67 (not_67_out, A0);
  not not_68 (not_68_out, A4);
  not not_69 (not_69_out, A1);
  not not_70 (not_70_out, A0);
  not not_71 (not_71_out, A0);
  not not_72 (not_72_out, A3);
  not not_73 (not_73_out, A1);
  not not_74 (not_74_out, A0);
  not not_75 (not_75_out, A4);
  not not_76 (not_76_out, A3);
  not not_77 (not_77_out, A1);
  not not_78 (not_78_out, A4);
  not not_79 (not_79_out, A3);
  not not_80 (not_80_out, A0);
  not not_81 (not_81_out, A2);
  not not_82 (not_82_out, A1);
  not not_83 (not_83_out, A0);
  not not_84 (not_84_out, A4);
  not not_85 (not_85_out, A3);
  not not_86 (not_86_out, A2);
  not not_87 (not_87_out, A1);
  not not_88 (not_88_out, A3);
  not not_89 (not_89_out, A2);
  not not_90 (not_90_out, A3);
  not not_91 (not_91_out, A0);
  not not_92 (not_92_out, A4);
  not not_93 (not_93_out, A1);
  not not_94 (not_94_out, A1);
  not not_95 (not_95_out, A4);
  not not_96 (not_96_out, A2);
  not not_97 (not_97_out, A0);
  not not_98 (not_98_out, A3);
  and and_1 (and_1_out, not_1_out, not_2_out, not_3_out);
  and and_2 (and_2_out, not_4_out, A1);
  and and_3 (and_3_out, not_5_out, A2, A0);
  and and_4 (and_4_out, not_6_out, A3, not_7_out);
  and and_5 (and_5_out, A3, A2, not_8_out);
  and and_6 (and_6_out, A4, not_9_out, not_10_out);
  and and_7 (and_7_out, A4, not_11_out, A0);
  and and_8 (and_8_out, A4, A1, not_12_out);
  and and_9 (and_9_out, not_13_out, not_14_out);
  and and_10 (and_10_out, not_15_out, not_16_out, not_17_out);
  and and_11 (and_11_out, not_18_out, not_19_out, A0);
  and and_12 (and_12_out, not_20_out, not_21_out, A1);
  and and_13 (and_13_out, not_22_out, A1, A0);
  and and_14 (and_14_out, not_23_out, A1, A0);
  and and_15 (and_15_out, not_24_out, A3, not_25_out);
  and and_16 (and_16_out, not_26_out, A3, not_27_out);
  and and_17 (and_17_out, A3, not_28_out, not_29_out);
  and and_18 (and_18_out, A4, A2);
  and and_19 (and_19_out, not_30_out, not_31_out);
  and and_20 (and_20_out, not_32_out, not_33_out);
  and and_21 (and_21_out, not_34_out, not_35_out, A2);
  and and_22 (and_22_out, A3, A1);
  and and_23 (and_23_out, A4, not_36_out);
  and and_24 (and_24_out, A4, not_37_out);
  and and_25 (and_25_out, not_38_out, not_39_out, not_40_out);
  and and_26 (and_26_out, not_41_out, not_42_out, not_43_out);
  and and_27 (and_27_out, not_44_out, not_45_out, A1);
  and and_28 (and_28_out, not_46_out, A1, not_47_out);
  and and_29 (and_29_out, not_48_out, A1, not_49_out);
  and and_30 (and_30_out, not_50_out, A2, not_51_out, A0);
  and and_31 (and_31_out, not_52_out, A3, not_53_out);
  and and_32 (and_32_out, A3, not_54_out, A0);
  and and_33 (and_33_out, not_55_out, A3, A2, A0);
  and and_34 (and_34_out, A4, not_56_out, A1);
  and and_35 (and_35_out, A4, A2, not_57_out);
  and and_36 (and_36_out, not_58_out, not_59_out, not_60_out);
  and and_37 (and_37_out, not_61_out, not_62_out, not_63_out);
  and and_38 (and_38_out, not_64_out, A1, not_65_out);
  and and_39 (and_39_out, not_66_out, A1, not_67_out);
  and and_40 (and_40_out, not_68_out, A3, not_69_out, not_70_out);
  and and_41 (and_41_out, A4, A2, not_71_out);
  and and_42 (and_42_out, not_72_out, not_73_out, not_74_out);
  and and_43 (and_43_out, not_75_out, not_76_out, A2, not_77_out);
  and and_44 (and_44_out, not_78_out, not_79_out, A2, not_80_out);
  and and_45 (and_45_out, A3, not_81_out, not_82_out);
  and and_46 (and_46_out, A3, A1, not_83_out);
  and and_47 (and_47_out, not_84_out, A3, A2, A1);
  and and_48 (and_48_out, A4, not_85_out, not_86_out, A1);
  and and_49 (and_49_out, A4, A3, not_87_out);
  and and_50 (and_50_out, not_88_out, not_89_out, A1);
  and and_51 (and_51_out, not_90_out, A1, not_91_out);
  and and_52 (and_52_out, not_92_out, A2, not_93_out);
  and and_53 (and_53_out, A3, not_94_out);
  and and_54 (and_54_out, not_95_out, A3, A2);
  and and_55 (and_55_out, A4, not_96_out, not_97_out);
  and and_56 (and_56_out, A4, not_98_out, A1);
  or or_1 (a, and_1_out, and_2_out, and_3_out, and_4_out, and_5_out, and_6_out, and_7_out, and_8_out);
  or or_2 (b, and_9_out, and_10_out, and_11_out, and_12_out, and_13_out, and_14_out, and_15_out, and_16_out, and_17_out, and_18_out);
  or or_3 (c, and_19_out, and_20_out, A0, and_21_out, and_22_out, and_23_out, and_24_out);
  or or_4 (d, and_25_out, and_26_out, and_27_out, and_28_out, and_29_out, and_30_out, and_31_out, and_32_out, and_33_out, and_34_out, and_35_out);
  or or_5 (e, and_36_out, and_37_out, and_38_out, and_39_out, and_40_out, and_41_out);
  or or_6 (f, and_42_out, and_43_out, and_44_out, and_45_out, and_46_out, and_47_out, and_48_out, and_49_out);
  or or_7 (g, and_50_out, and_51_out, and_52_out, and_53_out, and_54_out, and_55_out, and_56_out);
endmodule

module _7_segment2 (
  input  A4,
  input  A3,
  input  A2,
  input  A1,
  input  A0,
  output a,
  output b,
  output c,
  output d,
  output e,
  output f,
  output g
);

  wire and_1_out, and_2_out, and_3_out, and_4_out, and_5_out, and_6_out, and_7_out, and_8_out, and_9_out,
       and_10_out, and_11_out, and_12_out, and_13_out, and_14_out, and_15_out, and_16_out, and_17_out,
       and_18_out, and_19_out, not_1_out, not_2_out, not_3_out, not_4_out, not_5_out, not_6_out, not_7_out,
       not_8_out, not_9_out, not_10_out, not_11_out, not_12_out, not_13_out, not_14_out, not_15_out,
       not_16_out, not_17_out, not_18_out, not_19_out, not_20_out, not_21_out, not_22_out, not_23_out,
       not_24_out, not_25_out, not_26_out, not_27_out, not_28_out;

  not not_1 (not_1_out, A4);
  not not_2 (not_2_out, A3);
  not not_3 (not_3_out, A4);
  not not_4 (not_4_out, A2);
  not not_5 (not_5_out, A1);
  not not_6 (not_6_out, A3);
  not not_7 (not_7_out, A3);
  not not_8 (not_8_out, A2);
  not not_9 (not_9_out, A4);
  not not_10 (not_10_out, A3);
  not not_11 (not_11_out, A4);
  not not_12 (not_12_out, A2);
  not not_13 (not_13_out, A1);
  not not_14 (not_14_out, A3);
  not not_15 (not_15_out, A4);
  not not_16 (not_16_out, A3);
  not not_17 (not_17_out, A4);
  not not_18 (not_18_out, A2);
  not not_19 (not_19_out, A1);
  not not_20 (not_20_out, A3);
  not not_21 (not_21_out, A2);
  not not_22 (not_22_out, A1);
  not not_23 (not_23_out, A4);
  not not_24 (not_24_out, A3);
  not not_25 (not_25_out, A4);
  not not_26 (not_26_out, A2);
  not not_27 (not_27_out, A1);
  and and_1 (and_1_out, A4, A2);
  and and_2 (and_2_out, A4, A3);
  and and_3 (and_3_out, not_1_out, not_2_out);
  and and_4 (and_4_out, not_3_out, not_4_out, not_5_out);
  and and_5 (and_5_out, not_6_out, A2);
  and and_6 (and_6_out, A4, A3);
  not not_28 (not_28_out, A4);
  and and_7 (and_7_out, not_7_out, not_8_out);
  and and_8 (and_8_out, A3, A2, A1);
  and and_9 (and_9_out, not_9_out, not_10_out);
  and and_10 (and_10_out, not_11_out, not_12_out, not_13_out);
  and and_11 (and_11_out, not_14_out, A2);
  and and_12 (and_12_out, A4, A3);
  and and_13 (and_13_out, not_15_out, not_16_out);
  and and_14 (and_14_out, not_17_out, not_18_out, not_19_out);
  and and_15 (and_15_out, not_20_out, A2);
  and and_16 (and_16_out, A4, A3, not_21_out);
  and and_17 (and_17_out, A4, A3, not_22_out);
  and and_18 (and_18_out, not_23_out, not_24_out);
  and and_19 (and_19_out, not_25_out, not_26_out, not_27_out);
  or or_1 (g, and_1_out, and_2_out);
  or or_2 (a, and_3_out, and_4_out, and_5_out, and_6_out);
  or or_3 (c, not_28_out, and_7_out, and_8_out);
  or or_4 (d, and_9_out, and_10_out, and_11_out, and_12_out);
  or or_5 (e, and_13_out, and_14_out, and_15_out, and_16_out, and_17_out);
  or or_6 (f, and_18_out, and_19_out);

  assign b = 1'b1;
endmodule

module _7_segmentEnd (
  input  A0,
  output a,
  output b,
  output c,
  output d,
  output e,
  output f,
  output g
);

  not not_1 (a, A0);
  not not_2 (d, A0);
  not not_3 (e, A0);
  not not_4 (f, A0);

  assign b = 1'b1;
  assign c = 1'b1;
  assign g = 1'b0;
endmodule
